# Fritzing sketch Pong-connections (saved by Fritzing 0.9.3b)

parts:
  Componente1 = Arduino Mega 2560 (Rev3)
  U1 = HC-SR04 [chip_label=IC package="SIP (Single Inline) [THT]"]
  U2 = HC-SR04 [chip_label=IC package="SIP (Single Inline) [THT]"]
  Componente3 = Arduino Uno (Rev3)

nets:
  3V3: Componente1.3V3, U1.Vcc
  GND: Componente1.GND, U1.GND
  N1: Componente1.D2_PWM, U1.Trig
  N2: Componente1.D3_PWM, U1.Echo
  VCC: U2.Vcc, Componente3.3V3
  N3: U2.Trig, Componente3.D2
  N4: U2.Echo, Componente3.D3_PWM
  GND_2: U2.GND, Componente3.GND

custom parts:
  HC-SR04: HC-SR04 ultrasound distance sensor
